// Logisim project CIRCUITO REDUZIDO.circ as structural Verilog: 1 circuit, main circuit main
module main (
  input  A,
  input  B,
  input  C,
  input  D,
  output S
);

  wire and_1_out, and_2_out, and_3_out, or_1_out, or_2_out;

  or or_1 (or_1_out, B, C, D);
  or or_2 (or_2_out, C, D);
  and and_1 (and_1_out, A, or_1_out);
  and and_2 (and_2_out, B, or_2_out);
  or or_3 (S, and_1_out, and_2_out, and_3_out);
  and and_3 (and_3_out, C, D);
endmodule
