// Logisim project circuito s t.circ as structural Verilog: 1 circuit, main circuit main
module main (
  input  A,
  input  B,
  input  C,
  output S,
  output T
);

  wire nand_1_out, nand_2_out, not_1_out, or_1_out;

  nand nand_1 (nand_1_out, A, B);
  or or_1 (or_1_out, A, B);
  not not_1 (not_1_out, A);
  nand nand_2 (nand_2_out, C, not_1_out);
  or or_2 (S, nand_1_out, C);
  nand nand_3 (T, or_1_out, nand_2_out);
endmodule
