// Logisim project circuito1.circ as structural Verilog: 1 circuit, main circuit main
module main (
  input  A,
  input  B,
  input  C,
  input  D,
  output S
);

  wire and_1_out, and_2_out, and_3_out, and_4_out, and_5_out, and_6_out;

  and and_1 (and_1_out, C, D);
  and and_2 (and_2_out, B, D);
  and and_3 (and_3_out, B, C);
  and and_4 (and_4_out, A, D);
  and and_5 (and_5_out, A, C);
  and and_6 (and_6_out, A, B);
  or or_1 (S, and_1_out, and_2_out, and_3_out, and_4_out, and_5_out, and_6_out);
endmodule
