// Logisim project atividade aberta1.circ as structural Verilog: 1 circuit, main circuit main
module main (
  input  A,
  input  B,
  input  C,
  input  D,
  output S1,
  output S2
);

  wire and_1_out, not_1_out;

  not not_1 (not_1_out, A);
  and and_1 (and_1_out, not_1_out, C, D);
  or or_1 (S2, and_1_out, B);

  assign S1 = A;
endmodule
