// Logisim project Circuito Para praticar.circ as structural Verilog: 1 circuit, main circuit main
module main (
  input  L,
  input  U,
  input  Fd,
  input  Fe,
  output Abrir,
  output Fechar
);

  wire and_1_out, and_2_out, and_3_out, and_4_out, not_1_out, not_2_out, not_3_out, not_4_out, not_5_out;

  not not_1 (not_1_out, L);
  not not_2 (not_2_out, U);
  and and_1 (and_1_out, not_1_out, not_2_out, not_3_out);
  not not_3 (not_3_out, Fe);
  and and_2 (and_2_out, Fd, Fe);
  and and_3 (and_3_out, U, not_4_out);
  not not_4 (not_4_out, Fd);
  and and_4 (and_4_out, L, not_5_out);
  not not_5 (not_5_out, Fd);
  or or_1 (Abrir, and_1_out, and_2_out);
  or or_2 (Fechar, and_3_out, and_4_out);
endmodule
